// Logisim project main.circ as structural Verilog: 11 circuits, main circuit main
module main (
  input  in_1,
  input  in_2
);

  wire clock_1_out;
  wire [1:0] controller_1_as, controller_1_ir, controller_1_ram, controller_1_reg_b, controller_1_reg_out;
  wire [2:0] controller_1_mar, controller_1_reg_a;
  wire [3:0] binary_to_bcd_converter_1_p2, binary_to_bcd_converter_1_p3, binary_to_bcd_converter_1_p4,
       controller_1_sequencer;
  wire [7:0] accumulator_1_doutaddsub, controlled_buffer_1_out, controlled_buffer_2_out, controller_1_out_5,
       instruction_register_1_ictrl, memory_address_register_1_dram, multiplexer_1_out, out_reg_1_dout,
       ram_1_dout, reg_b_1_dout;

  Clock clock_1 (.out(clock_1_out));
  RAM #(.enables("line"), .\type ("nonvolatile")) ram_1 (
    .addr(multiplexer_1_out), .we(controller_1_ram[1]), .clk(clock_1_out), .din(controlled_buffer_1_out),
    .dout(ram_1_dout));
  assign controlled_buffer_1_out = controller_1_ram[1] ? controlled_buffer_2_out : 8'bz;  // Controlled_Buffer controlled_buffer_1
  assign controlled_buffer_2_out = controller_1_ram[0] ? ram_1_dout : 8'bz;  // Controlled_Buffer controlled_buffer_2
  Multiplexer #(.width(8)) multiplexer_1 (
    .in0(memory_address_register_1_dram), .in1(controller_1_out_5), .out(multiplexer_1_out),
    .sel(controller_1_ram[0]));
  program_counter program_counter_1 (
    .initINC(controller_1_sequencer[0]), .enSEQUENCE(controller_1_sequencer[3]),
    .instADDR(controlled_buffer_2_out), .cJUMP(controller_1_sequencer[1]), .clk(clock_1_out),
    .reset(controller_1_sequencer[2]), .incOUT(controlled_buffer_2_out));
  memory_address_register memory_address_register_1 (
    .dBUS(controlled_buffer_2_out), .enMAR(controller_1_mar[0]), .clk(clock_1_out),
    .reset(controller_1_mar[1]), .in_5(controller_1_mar[2]), .dRAM(memory_address_register_1_dram));
  instruction_register instruction_register_1 (
    .iBUS(controlled_buffer_2_out), .clkFETCH(controller_1_ir[0]), .clk(clock_1_out),
    .reset(controller_1_ir[1]), .iCTRL(instruction_register_1_ictrl));
  controller controller_1 (
    .dataIR(instruction_register_1_ictrl), .stepENABLE(in_1), .CLK(clock_1_out), .reset(in_2),
    .out_5(controller_1_out_5), .REG_A(controller_1_reg_a), .AS(controller_1_as), .REG_B(controller_1_reg_b),
    .REG_OUT(controller_1_reg_out), .SEQUENCER(controller_1_sequencer), .MAR(controller_1_mar),
    .RAM(controller_1_ram), .IR(controller_1_ir));
  accumulator accumulator_1 (
    .dINBUS(controlled_buffer_2_out), .load(controller_1_reg_a[0]), .clk(clock_1_out),
    .reset(controller_1_reg_a[2]), .store(controller_1_reg_a[1]), .dOUTBUS(controlled_buffer_2_out),
    .dOUTADDSUB(accumulator_1_doutaddsub));
  adder_subtractor adder_subtractor_1 (
    .cSUB(controller_1_as[0]), .B(reg_b_1_dout), .A(accumulator_1_doutaddsub), .enAS(controller_1_as[1]),
    .Result(controlled_buffer_2_out));  // open: fZERO, fNEG
  reg_b reg_b_1 (
    .dIN(controlled_buffer_2_out), .LOAD(controller_1_reg_b[0]), .clk(clock_1_out),
    .reset(controller_1_reg_b[1]), .dOUT(reg_b_1_dout));
  out_reg out_reg_1 (
    .dIN(controlled_buffer_2_out), .outLOAD(controller_1_reg_out[0]), .clk(clock_1_out),
    .reset(controller_1_reg_out[1]), .dOUT(out_reg_1_dout));
  Hex_Digit_Display hex_digit_display_1 (.value(binary_to_bcd_converter_1_p2));  // open: dp
  // Binary_to_BCD_converter #(.binvalue(8)) binary_to_bcd_converter_1: pin names not known; wires that end beside it: out_reg_1_dout, binary_to_bcd_converter_1_p2, binary_to_bcd_converter_1_p3, binary_to_bcd_converter_1_p4
  Hex_Digit_Display hex_digit_display_2 (.value(binary_to_bcd_converter_1_p3));  // open: dp
  Hex_Digit_Display hex_digit_display_3 (.value(binary_to_bcd_converter_1_p4));  // open: dp
endmodule

module adder_subtractor (
  input  cSUB,
  input  [7:0] B,
  input  [7:0] A,
  input  enAS,
  output [7:0] Result,
  output fZERO,
  output fNEG
);

  wire full_adder_1_cout, full_adder_2_cout, full_adder_3_cout, full_adder_4_cout, full_adder_5_cout,
       full_adder_6_cout, full_adder_7_cout, xor_1_out, xor_2_out, xor_3_out, xor_4_out, xor_5_out,
       xor_6_out, xor_7_out, xor_8_out;
  wire [6:0] full_adder_1_s;

  xor xor_1 (xor_1_out, B[7], cSUB);
  xor xor_2 (xor_2_out, B[6], cSUB);
  xor xor_3 (xor_3_out, B[5], cSUB);
  xor xor_4 (xor_4_out, B[4], cSUB);
  xor xor_5 (xor_5_out, B[3], cSUB);
  xor xor_6 (xor_6_out, B[2], cSUB);
  xor xor_7 (xor_7_out, B[1], cSUB);
  xor xor_8 (xor_8_out, B[0], cSUB);
  full_adder full_adder_1 (.A(A[0]), .B(xor_8_out), .C(cSUB), .S(full_adder_1_s[0]), .Cout(full_adder_1_cout));
  full_adder full_adder_2 (
    .A(A[1]), .B(xor_7_out), .C(full_adder_1_cout), .S(full_adder_1_s[1]), .Cout(full_adder_2_cout));
  full_adder full_adder_3 (
    .A(A[2]), .B(xor_6_out), .C(full_adder_2_cout), .S(full_adder_1_s[2]), .Cout(full_adder_3_cout));
  full_adder full_adder_4 (
    .A(A[3]), .B(xor_5_out), .C(full_adder_3_cout), .S(full_adder_1_s[3]), .Cout(full_adder_4_cout));
  full_adder full_adder_5 (
    .A(A[4]), .B(xor_4_out), .C(full_adder_4_cout), .S(full_adder_1_s[4]), .Cout(full_adder_5_cout));
  full_adder full_adder_6 (
    .A(A[5]), .B(xor_3_out), .C(full_adder_5_cout), .S(full_adder_1_s[5]), .Cout(full_adder_6_cout));
  full_adder full_adder_7 (
    .A(A[6]), .B(xor_2_out), .C(full_adder_6_cout), .S(full_adder_1_s[6]), .Cout(full_adder_7_cout));
  full_adder full_adder_8 (.A(A[7]), .B(xor_1_out), .C(full_adder_7_cout), .S(fNEG));  // open: Cout
  nor nor_1 (fZERO, full_adder_1_s[0], full_adder_1_s[1], full_adder_1_s[2], full_adder_1_s[3], full_adder_1_s[4], full_adder_1_s[5], full_adder_1_s[6], fNEG);
  assign Result = enAS ? {fNEG, full_adder_1_s} : 8'bz;  // Controlled_Buffer controlled_buffer_1
endmodule

module full_adder (
  input  A,
  input  B,
  input  C,
  output S,
  output Cout
);

  wire and_1_out, and_2_out, xor_1_out;

  xor xor_1 (xor_1_out, A, B);
  and and_1 (and_1_out, A, B);
  xor xor_2 (S, xor_1_out, C);
  and and_2 (and_2_out, xor_1_out, C);
  or or_1 (Cout, and_2_out, and_1_out);
endmodule

module program_counter (
  input  [7:0] instADDR,
  input  cJUMP,
  input  initINC,
  input  clk,
  input  reset,
  input  enSEQUENCE,
  output [7:0] incOUT
);

  wire half_adder_1_cout, half_adder_2_cout, half_adder_3_cout, half_adder_4_cout, half_adder_5_cout,
       half_adder_6_cout, half_adder_7_cout, half_adder_8_cout, not_1_out;
  wire [7:0] d_ff_8_q, half_adder_8_sum, multiplexer_1_out;

  Multiplexer #(.width(8)) multiplexer_1 (.in0(half_adder_8_sum), .in1(instADDR), .out(multiplexer_1_out), .sel(cJUMP));
  half_adder half_adder_1 (.A(d_ff_8_q[7]), .B(half_adder_2_cout), .Sum(half_adder_8_sum[7]), .Cout(half_adder_1_cout));
  D_Flip_Flop d_ff_1 (.D(multiplexer_1_out[7]), .clk(not_1_out), .Q(d_ff_8_q[7]), .reset(reset));  // open: Qn, preset
  not not_1 (not_1_out, clk);
  half_adder half_adder_2 (.A(d_ff_8_q[6]), .B(half_adder_3_cout), .Sum(half_adder_8_sum[6]), .Cout(half_adder_2_cout));
  D_Flip_Flop d_ff_2 (.D(multiplexer_1_out[6]), .clk(not_1_out), .Q(d_ff_8_q[6]), .reset(reset));  // open: Qn, preset
  half_adder half_adder_3 (.A(d_ff_8_q[5]), .B(half_adder_4_cout), .Sum(half_adder_8_sum[5]), .Cout(half_adder_3_cout));
  D_Flip_Flop d_ff_3 (.D(multiplexer_1_out[5]), .clk(not_1_out), .Q(d_ff_8_q[5]), .reset(reset));  // open: Qn, preset
  half_adder half_adder_4 (.A(d_ff_8_q[4]), .B(half_adder_5_cout), .Sum(half_adder_8_sum[4]), .Cout(half_adder_4_cout));
  D_Flip_Flop d_ff_4 (.D(multiplexer_1_out[4]), .clk(not_1_out), .Q(d_ff_8_q[4]), .reset(reset));  // open: Qn, preset
  half_adder half_adder_5 (.A(d_ff_8_q[3]), .B(half_adder_6_cout), .Sum(half_adder_8_sum[3]), .Cout(half_adder_5_cout));
  D_Flip_Flop d_ff_5 (.D(multiplexer_1_out[3]), .clk(not_1_out), .Q(d_ff_8_q[3]), .reset(reset));  // open: Qn, preset
  half_adder half_adder_6 (.A(d_ff_8_q[2]), .B(half_adder_7_cout), .Sum(half_adder_8_sum[2]), .Cout(half_adder_6_cout));
  D_Flip_Flop d_ff_6 (.D(multiplexer_1_out[2]), .clk(not_1_out), .Q(d_ff_8_q[2]), .reset(reset));  // open: Qn, preset
  half_adder half_adder_7 (.A(d_ff_8_q[1]), .B(half_adder_8_cout), .Sum(half_adder_8_sum[1]), .Cout(half_adder_7_cout));
  D_Flip_Flop d_ff_7 (.D(multiplexer_1_out[1]), .clk(not_1_out), .Q(d_ff_8_q[1]), .reset(reset));  // open: Qn, preset
  half_adder half_adder_8 (.A(d_ff_8_q[0]), .B(initINC), .Sum(half_adder_8_sum[0]), .Cout(half_adder_8_cout));
  D_Flip_Flop d_ff_8 (.D(multiplexer_1_out[0]), .clk(not_1_out), .Q(d_ff_8_q[0]), .reset(reset));  // open: Qn, preset
  assign incOUT = enSEQUENCE ? d_ff_8_q : 8'bz;  // Controlled_Buffer controlled_buffer_1
  // also tied to GND on the sheet: half_adder_1_cout

  // Notes on the sheet:
  //   Chooses either JUMP or INCREMENT
  //   Incrementation: Addition of previous state. Hence the half-adders
endmodule

module half_adder (
  input  A,
  input  B,
  output Sum,
  output Cout
);

  xor xor_1 (Sum, A, B);
  and and_1 (Cout, A, B);
endmodule

module accumulator (
  input  [7:0] dINBUS,
  input  load,
  input  clk,
  input  reset,
  input  store,
  output [7:0] dOUTBUS,
  output [7:0] dOUTADDSUB
);

  wire [7:0] controlled_buffer_1_out;

  assign controlled_buffer_1_out = load ? dINBUS : 8'bz;  // Controlled_Buffer controlled_buffer_1
  D_Flip_Flop d_ff_1 (.D(controlled_buffer_1_out[0]), .clk(clk), .Q(dOUTADDSUB[0]), .reset(reset));  // open: Qn, preset
  D_Flip_Flop d_ff_2 (.D(controlled_buffer_1_out[1]), .clk(clk), .Q(dOUTADDSUB[1]), .reset(reset));  // open: Qn, preset
  D_Flip_Flop d_ff_3 (.D(controlled_buffer_1_out[2]), .clk(clk), .Q(dOUTADDSUB[2]), .reset(reset));  // open: Qn, preset
  D_Flip_Flop d_ff_4 (.D(controlled_buffer_1_out[3]), .clk(clk), .Q(dOUTADDSUB[3]), .reset(reset));  // open: Qn, preset
  D_Flip_Flop d_ff_5 (.D(controlled_buffer_1_out[4]), .clk(clk), .Q(dOUTADDSUB[4]), .reset(reset));  // open: Qn, preset
  D_Flip_Flop d_ff_6 (.D(controlled_buffer_1_out[5]), .clk(clk), .Q(dOUTADDSUB[5]), .reset(reset));  // open: Qn, preset
  D_Flip_Flop d_ff_7 (.D(controlled_buffer_1_out[6]), .clk(clk), .Q(dOUTADDSUB[6]), .reset(reset));  // open: Qn, preset
  D_Flip_Flop d_ff_8 (.D(controlled_buffer_1_out[7]), .clk(clk), .Q(dOUTADDSUB[7]), .reset(reset));  // open: Qn, preset
  assign dOUTBUS = store ? dOUTADDSUB : 8'bz;  // Controlled_Buffer controlled_buffer_2

  // Notes on the sheet:
  //   Another big register
  //   Can output to BUS
endmodule

module instruction_register (
  input  [7:0] iBUS,
  input  clkFETCH,
  input  clk,
  input  reset,
  output [7:0] iCTRL
);

  wire [7:0] controlled_buffer_1_out;

  assign controlled_buffer_1_out = clkFETCH ? iBUS : 8'bz;  // Controlled_Buffer controlled_buffer_1
  D_Flip_Flop d_ff_1 (.D(controlled_buffer_1_out[0]), .clk(clk), .Q(iCTRL[0]), .reset(reset));  // open: Qn, preset
  D_Flip_Flop d_ff_2 (.D(controlled_buffer_1_out[1]), .clk(clk), .Q(iCTRL[1]), .reset(reset));  // open: Qn, preset
  D_Flip_Flop d_ff_3 (.D(controlled_buffer_1_out[2]), .clk(clk), .Q(iCTRL[2]), .reset(reset));  // open: Qn, preset
  D_Flip_Flop d_ff_4 (.D(controlled_buffer_1_out[3]), .clk(clk), .Q(iCTRL[3]), .reset(reset));  // open: Qn, preset
  D_Flip_Flop d_ff_5 (.D(controlled_buffer_1_out[4]), .clk(clk), .Q(iCTRL[4]), .reset(reset));  // open: Qn, preset
  D_Flip_Flop d_ff_6 (.D(controlled_buffer_1_out[5]), .clk(clk), .Q(iCTRL[5]), .reset(reset));  // open: Qn, preset
  D_Flip_Flop d_ff_7 (.D(controlled_buffer_1_out[6]), .clk(clk), .Q(iCTRL[6]), .reset(reset));  // open: Qn, preset
  D_Flip_Flop d_ff_8 (.D(controlled_buffer_1_out[7]), .clk(clk), .Q(iCTRL[7]), .reset(reset));  // open: Qn, preset
endmodule

module memory_address_register (
  input  [7:0] dBUS,
  input  enMAR,
  input  clk,
  input  reset,
  input  in_5,
  output [7:0] dRAM
);

  wire [7:0] controlled_buffer_1_out, d_ff_1_q;

  assign controlled_buffer_1_out = enMAR ? dBUS : 8'bz;  // Controlled_Buffer controlled_buffer_1
  D_Flip_Flop d_ff_1 (.D(controlled_buffer_1_out[0]), .clk(clk), .Q(d_ff_1_q[0]), .reset(reset));  // open: Qn, preset
  D_Flip_Flop d_ff_2 (.D(controlled_buffer_1_out[1]), .clk(clk), .Q(d_ff_1_q[1]), .reset(reset));  // open: Qn, preset
  D_Flip_Flop d_ff_3 (.D(controlled_buffer_1_out[2]), .clk(clk), .Q(d_ff_1_q[2]), .reset(reset));  // open: Qn, preset
  D_Flip_Flop d_ff_4 (.D(controlled_buffer_1_out[3]), .clk(clk), .Q(d_ff_1_q[3]), .reset(reset));  // open: Qn, preset
  D_Flip_Flop d_ff_5 (.D(controlled_buffer_1_out[4]), .clk(clk), .Q(d_ff_1_q[4]), .reset(reset));  // open: Qn, preset
  D_Flip_Flop d_ff_6 (.D(controlled_buffer_1_out[5]), .clk(clk), .Q(d_ff_1_q[5]), .reset(reset));  // open: Qn, preset
  D_Flip_Flop d_ff_7 (.D(controlled_buffer_1_out[6]), .clk(clk), .Q(d_ff_1_q[6]), .reset(reset));  // open: Qn, preset
  D_Flip_Flop d_ff_8 (.D(controlled_buffer_1_out[7]), .clk(clk), .Q(d_ff_1_q[7]), .reset(reset));  // open: Qn, preset
  assign dRAM = in_5 ? d_ff_1_q : 8'bz;  // Controlled_Buffer controlled_buffer_2

  // Notes on the sheet:
  //   Another big register
endmodule

module reg_b (
  input  [7:0] dIN,
  input  LOAD,
  input  clk,
  input  reset,
  output [7:0] dOUT
);

  wire [7:0] controlled_buffer_1_out;

  assign controlled_buffer_1_out = LOAD ? dIN : 8'bz;  // Controlled_Buffer controlled_buffer_1
  D_Flip_Flop d_ff_1 (.D(controlled_buffer_1_out[0]), .clk(clk), .Q(dOUT[0]), .reset(reset));  // open: Qn, preset
  D_Flip_Flop d_ff_2 (.D(controlled_buffer_1_out[1]), .clk(clk), .Q(dOUT[1]), .reset(reset));  // open: Qn, preset
  D_Flip_Flop d_ff_3 (.D(controlled_buffer_1_out[2]), .clk(clk), .Q(dOUT[2]), .reset(reset));  // open: Qn, preset
  D_Flip_Flop d_ff_4 (.D(controlled_buffer_1_out[3]), .clk(clk), .Q(dOUT[3]), .reset(reset));  // open: Qn, preset
  D_Flip_Flop d_ff_5 (.D(controlled_buffer_1_out[4]), .clk(clk), .Q(dOUT[4]), .reset(reset));  // open: Qn, preset
  D_Flip_Flop d_ff_6 (.D(controlled_buffer_1_out[5]), .clk(clk), .Q(dOUT[5]), .reset(reset));  // open: Qn, preset
  D_Flip_Flop d_ff_7 (.D(controlled_buffer_1_out[6]), .clk(clk), .Q(dOUT[6]), .reset(reset));  // open: Qn, preset
  D_Flip_Flop d_ff_8 (.D(controlled_buffer_1_out[7]), .clk(clk), .Q(dOUT[7]), .reset(reset));  // open: Qn, preset

  // Notes on the sheet:
  //   Another big register
endmodule

module out_reg (
  input  [7:0] dIN,
  input  outLOAD,
  input  clk,
  input  reset,
  output [7:0] dOUT
);

  wire [7:0] controlled_buffer_1_out;

  assign controlled_buffer_1_out = outLOAD ? dIN : 8'bz;  // Controlled_Buffer controlled_buffer_1
  D_Flip_Flop d_ff_1 (.D(controlled_buffer_1_out[0]), .clk(clk), .Q(dOUT[0]), .reset(reset));  // open: Qn, preset
  D_Flip_Flop d_ff_2 (.D(controlled_buffer_1_out[1]), .clk(clk), .Q(dOUT[1]), .reset(reset));  // open: Qn, preset
  D_Flip_Flop d_ff_3 (.D(controlled_buffer_1_out[2]), .clk(clk), .Q(dOUT[2]), .reset(reset));  // open: Qn, preset
  D_Flip_Flop d_ff_4 (.D(controlled_buffer_1_out[3]), .clk(clk), .Q(dOUT[3]), .reset(reset));  // open: Qn, preset
  D_Flip_Flop d_ff_5 (.D(controlled_buffer_1_out[4]), .clk(clk), .Q(dOUT[4]), .reset(reset));  // open: Qn, preset
  D_Flip_Flop d_ff_6 (.D(controlled_buffer_1_out[5]), .clk(clk), .Q(dOUT[5]), .reset(reset));  // open: Qn, preset
  D_Flip_Flop d_ff_7 (.D(controlled_buffer_1_out[6]), .clk(clk), .Q(dOUT[6]), .reset(reset));  // open: Qn, preset
  D_Flip_Flop d_ff_8 (.D(controlled_buffer_1_out[7]), .clk(clk), .Q(dOUT[7]), .reset(reset));  // open: Qn, preset
endmodule

module controller (
  input  [7:0] dataIR,
  input  stepENABLE,
  input  CLK,
  input  reset,
  output [7:0] out_5,
  output [3:0] SEQUENCER,
  output [2:0] REG_A,
  output [2:0] MAR,
  output [1:0] AS,
  output [1:0] RAM,
  output [1:0] REG_B,
  output [1:0] IR,
  output [1:0] REG_OUT
);

  wire and_5_out, and_6_out, d_ff_1_q, d_ff_2_q, half_adder_1_sum, half_adder_2_cout, half_adder_2_sum,
       nor_1_out, nor_2_out, nor_3_out, nor_4_out, nor_5_out, nor_7_out, nor_8_out, nor_9_out, nor_14_out,
       or_1_out;

  and and_1 (SEQUENCER[3], stepENABLE, nor_1_out);
  and and_2 (RAM[0], ~SEQUENCER[3], or_1_out);  // AND_Gate
  half_adder half_adder_1 (.A(d_ff_1_q), .B(half_adder_2_cout), .Sum(half_adder_1_sum));  // open: Cout
  D_Flip_Flop d_ff_1 (.D(half_adder_1_sum), .clk(CLK), .Q(d_ff_1_q), .reset(reset));  // open: Qn, preset
  nor nor_1 (nor_1_out, d_ff_1_q, d_ff_2_q);
  and and_3 (IR[0], ~d_ff_1_q, d_ff_2_q);  // AND_Gate
  and and_4 (MAR[0], SEQUENCER[3], or_1_out);
  half_adder half_adder_2 (.A(d_ff_2_q), .B(and_5_out), .Sum(half_adder_2_sum), .Cout(half_adder_2_cout));
  D_Flip_Flop d_ff_2 (.D(half_adder_2_sum), .clk(CLK), .Q(d_ff_2_q), .reset(reset));  // open: Qn, preset
  and and_5 (and_5_out, stepENABLE, ~and_6_out);  // AND_Gate
  and and_6 (and_6_out, nor_2_out, d_ff_1_q);
  or or_1 (or_1_out, IR[0], nor_3_out, SEQUENCER[3], nor_4_out, nor_5_out, RAM[1]);
  or or_2 (SEQUENCER[1], nor_7_out, nor_8_out, nor_9_out);
  nor nor_2 (nor_2_out, dataIR[7], dataIR[6], dataIR[5], dataIR[4]);
  nor nor_3 (nor_3_out, dataIR[7], dataIR[6], dataIR[5], ~dataIR[4]);  // NOR_Gate
  nor nor_4 (nor_4_out, dataIR[7], dataIR[6], ~dataIR[5], dataIR[4]);  // NOR_Gate
  nor nor_5 (nor_5_out, dataIR[7], dataIR[6], ~dataIR[5], ~dataIR[4]);  // NOR_Gate
  nor nor_6 (RAM[1], dataIR[7], ~dataIR[6], dataIR[5], dataIR[4]);  // NOR_Gate
  nor nor_7 (nor_7_out, dataIR[7], ~dataIR[6], ~dataIR[5], ~dataIR[4]);  // NOR_Gate
  nor nor_8 (nor_8_out, ~dataIR[7], dataIR[6], dataIR[5], ~dataIR[4]);  // NOR_Gate
  nor nor_9 (nor_9_out, ~dataIR[7], dataIR[6], ~dataIR[5], dataIR[4]);  // NOR_Gate
  nor nor_10 (REG_A[0], dataIR[7], dataIR[6], dataIR[5], ~dataIR[4]);  // NOR_Gate
  nor nor_11 (AS[0], dataIR[7], dataIR[6], ~dataIR[5], dataIR[4]);  // NOR_Gate
  nor nor_12 (REG_OUT[0], dataIR[7], dataIR[6], ~dataIR[5], ~dataIR[4]);  // NOR_Gate
  nor nor_13 (REG_A[1], dataIR[7], ~dataIR[6], dataIR[5], dataIR[4]);  // NOR_Gate
  nor nor_14 (nor_14_out, dataIR[7], ~dataIR[6], dataIR[5], ~dataIR[4]);  // NOR_Gate
  nor nor_15 (REG_B[1], dataIR[7], ~dataIR[6], ~dataIR[5], dataIR[4]);  // NOR_Gate
  or or_3 (REG_B[0], nor_14_out, REG_B[1]);
  assign out_5 = d_ff_1_q ? {4'b0000, dataIR[3:0]} : 8'bz;  // Controlled_Buffer controlled_buffer_1

  assign AS[1] = reset;
  assign IR[1] = reset;
  assign MAR[2:1] = {IR[0], reset};
  assign REG_A[2] = reset;
  assign REG_OUT[1] = reset;
  assign {SEQUENCER[2], SEQUENCER[0]} = {reset, SEQUENCER[3]};
endmodule
